// Logisim project main.circ as structural Verilog: 9 circuits, main circuit am08x24arc-main
module am08x24arc_main (
  input  in_1,
  input  in_2,
  output [15:0] DATA_BUS_STATUS,
  output [15:0] RAM_STATUS,
  output [15:0] out_5,
  output [15:0] ALU_STATUS,
  output [7:0] out_7,
  output [3:0] out_8,
  output [15:0] out_9,
  output [2:0] out_10,
  output [15:0] out_11,
  output [15:0] out_12
);

  wire ALU_SRC, and_1_out, and_2_out, and_3_out, and_4_out, and_5_out, and_6_out, CLOCK, clock_1_out,
       comparator_1_eq, comparator_1_gt, comparator_1_lt, HALT, I_O_SRC, INC_PC, JNEG, JPOS, JZ, not_1_out,
       not_2_out, not_3_out, OPERAND_SRC, or_2_out, PC_ADRESS_WRITE, PC_SRC, RAM_SRC, STACK_NEXT_SRC,
       STACK_POP, STACK_SWAP, STACK_TOP_SRC, t_ff_1_q, t_ff_1_qn, t_ff_2_q, t_ff_2_qn;
  wire [10:4] controlled_buffer_7_out;
  wire [15:0] controlled_buffer_1_out, STORED_ON_STACK;

  assign controlled_buffer_1_out = out_7[6] ? out_9 : 16'bz;  // Controlled_Buffer controlled_buffer_1
  assign controlled_buffer_1_out = ~out_7[6] ? DATA_BUS_STATUS : 16'bz;  // Controlled_Buffer controlled_buffer_2
  Clock clock_1 (.out(clock_1_out));
  and and_1 (and_1_out, ~out_7[6], out_7[4]);  // AND_Gate
  and and_2 (and_2_out, out_7[6], out_7[4], or_2_out);
  or or_1 (PC_ADRESS_WRITE, and_1_out, and_2_out);
  and and_3 (and_3_out, clock_1_out, ~HALT, ~in_2);  // AND_Gate
  LED led_1 (.in(in_2));
  Comparator #(.width(16)) comparator_1 (
    .a(out_12), .b({16{1'b0}}), .gt(comparator_1_gt), .eq(comparator_1_eq), .lt(comparator_1_lt));
  or or_2 (or_2_out, and_5_out, and_4_out, and_6_out);
  Counter #(.width(16), .max('hffff), .ongoal("stay")) PC (
    .load(PC_ADRESS_WRITE), .D(controlled_buffer_1_out), .Q(out_11), .clk(INC_PC));  // open: count, carry, clr, preset, down
  not not_1 (not_1_out, and_3_out);
  and and_4 (and_4_out, comparator_1_eq, JZ);
  and and_5 (and_5_out, comparator_1_gt, JPOS);
  T_Flip_Flop t_ff_1 (.clk(not_1_out), .T(1'b1), .Q(t_ff_1_q), .Qn(t_ff_1_qn));  // open: preset, reset
  T_Flip_Flop #(.Pre_Clr_Positions("LEGACY"), .enable("true")) t_ff_2 (
    .clk(and_3_out), .T(1'b1), .Q(t_ff_2_q), .Qn(t_ff_2_qn));  // open: preset, reset, en
  and and_6 (and_6_out, comparator_1_lt, JNEG);
  and and_7 (CLOCK, and_3_out, t_ff_1_qn, t_ff_2_q);
  and and_8 (INC_PC, t_ff_2_qn, t_ff_1_q, and_3_out);
  assign DATA_BUS_STATUS = PC_SRC ? out_11 : 16'bz;  // Controlled_Buffer controlled_buffer_3
  assign DATA_BUS_STATUS = OPERAND_SRC ? out_5 : 16'bz;  // Controlled_Buffer controlled_buffer_4
  ROM #(.addrWidth(16), .dataWidth(24), .Select("low")) Program (.addr(out_11), .data({out_7, out_5}));
  // Probe on out_9
  // Probe on out_12
  // Probe on STORED_ON_STACK
  not not_2 (not_2_out, out_7[5]);
  RAM #(.addrWidth(16), .dataWidth(16), .Select("low")) DATA (
    .addr(out_9), .data(DATA_BUS_STATUS), .sel(not_2_out), .clk(CLOCK), .ld(RAM_SRC));  // open: clr
  // Probe on out_11
  LED led_2 (.in(PC_ADRESS_WRITE));
  am08x24arc_stack am08x24arc_stack_1 (
    .DATA_IN(DATA_BUS_STATUS), .PUSH(out_7[7]), .POP(STACK_POP), .SWAP(STACK_SWAP), .TOP(out_9),
    .NEXT(out_12), .SEL(in_1), .CLOCK(CLOCK), .STORED(STORED_ON_STACK));
  Decoder #(.select(3), .enable("false")) decoder_1 (
    .out0(OPERAND_SRC), .out1(RAM_SRC), .out2(ALU_SRC), .out3(I_O_SRC), .out4(PC_SRC), .out5(STACK_TOP_SRC),
    .out6(STACK_NEXT_SRC), .sel(out_7[2:0]));  // open: out7
  assign DATA_BUS_STATUS = STACK_TOP_SRC ? out_9 : 16'bz;  // Controlled_Buffer controlled_buffer_5
  assign DATA_BUS_STATUS = STACK_NEXT_SRC ? out_12 : 16'bz;  // Controlled_Buffer controlled_buffer_6
  not not_3 (not_3_out, out_7[6]);
  assign {STACK_POP, STACK_SWAP, JZ, JNEG, JPOS, controlled_buffer_7_out, out_8} = not_3_out ? {16{1'b0}} : 16'bz;  // Controlled_Buffer controlled_buffer_7
  assign {STACK_POP, STACK_SWAP, JZ, JNEG, JPOS, controlled_buffer_7_out, out_8} = out_7[6] ? out_5 : 16'bz;  // Controlled_Buffer controlled_buffer_8
  alu alu_1 (.A(out_9), .B(out_12), .ALU_OP(out_8), .OUT(ALU_STATUS));  // open: CARRY_IN, ZF, CF
  assign DATA_BUS_STATUS = ALU_SRC ? ALU_STATUS : 16'bz;  // Controlled_Buffer controlled_buffer_9
  nor nor_1 (HALT, out_7[0], out_7[1], out_7[2], out_7[3], out_7[4], out_7[5], out_7[6], out_7[7]);

  assign out_10 = out_7[2:0];

  // Other names for the same wires on the sheet: ARGUMENT[15:0] = out_5; OPCODE[7:0] = out_7; SRC[2:0] = out_7[2:0];
  //   PC = out_7[4]; RAM = out_7[5]; _24BIT_INSTUCTION = out_7[6]; STACK_PUSH = out_7[7]; ALU_OP[3:0] = out_8;
  //   ALU_OUT[15:0] = ALU_STATUS; BADOP = in_2; DATA_BUS[15:0] = DATA_BUS_STATUS; PROGRAM_COUNTER[15:0] = out_11;
  //   RAM_VALUE[15:0] = RAM_STATUS; STACK_NEXT[15:0] = out_12; STACK_TOP[15:0] = out_9

  // Notes on the sheet:
  //   PROGRAM COUNTER
  //   CLOCK
  //   Conditional jumps
  //   ROM
  //   contents of Program (hex, n*v repeats v):
  //   100001 800000 800001 c50000 80fff0 660000 408000 408000 80fff1 660000 408000 408000 80fff2 660000
  //   408000 408000 80fff1 e10000 404000 408000 80fff2 e10000 404000 408000 80fff0 e10000 404000 408000
  //   c20000 404000 408000 404000 408000 100003
  //   STACK STATUS
  //   COMPUTER STATUS
  //   INSTRUCTION STATUS
  //   RAM
  //   PC STATUS
  //   am08x24arc-main
  //   STACK
  //   SOURCE DECODER
  //   DECODER
  //   ALU
  //   HALT
endmodule

// ALU
module alu (
  input  [15:0] A,
  input  [15:0] B,
  input  [3:0] ALU_OP,
  input  CARRY_IN,
  output [15:0] OUT,
  output ZF,
  output CF
);

  wire [15:0] adder_1_out, adder_2_out, and_1_out, nand_1_out, negator_1_out, nor_1_out, not_1_out, or_1_out,
       subtractor_1_out, subtractor_2_out, xor_1_out;

  Adder #(.width(16)) adder_1 (.a(A), .b(B), .out(adder_1_out));  // open: cin, cout
  Adder #(.width(16)) adder_2 (.a(A), .b(B), .out(adder_2_out), .cin(CARRY_IN));  // open: cout
  Subtractor #(.width(16)) subtractor_1 (.a(A), .b(B), .out(subtractor_1_out));  // open: bin, bout
  Subtractor #(.width(16)) subtractor_2 (.a(A), .b(B), .out(subtractor_2_out), .bin(CARRY_IN));  // open: bout
  Comparator #(.width(16)) comparator_1 (.a(A), .b(B), .eq(ZF), .lt(CF));  // open: gt
  Negator #(.width(16)) negator_1 (.in(A), .out(negator_1_out));
  assign not_1_out = ~A;  // NOT_Gate not_1, 16 bits wide
  assign and_1_out = A & B;  // AND_Gate and_1, 16 bits wide
  assign or_1_out = A | B;  // OR_Gate or_1, 16 bits wide
  assign nand_1_out = ~(A & B);  // NAND_Gate nand_1, 16 bits wide
  assign nor_1_out = ~(A | B);  // NOR_Gate nor_1, 16 bits wide
  assign xor_1_out = A ^ B;  // XOR_Gate xor_1, 16 bits wide
  Multiplexer #(.select(4), .width(16), .enable("false")) multiplexer_1 (
    .in0(adder_1_out), .in1(adder_2_out), .in2(subtractor_1_out), .in3(subtractor_2_out),
    .in4(negator_1_out), .in5(not_1_out), .in6(and_1_out), .in7(or_1_out), .in8(nand_1_out), .in9(nor_1_out),
    .in10(xor_1_out), .out(OUT), .sel(ALU_OP));  // open: in11, in12, in13, in14, in15

  // Notes on the sheet:
  //   ALU interface
endmodule

// STACK
module stack (
  input  [15:0] IN,
  input  PUSH,
  input  POP,
  input  SEL,
  input  CLOCK,
  output [15:0] TOP,
  output [15:0] NEXT,
  output HAS_NEXT,
  output OVERFLOW
);

  wire decoder_1_out0, decoder_1_out1, decoder_1_out2, decoder_1_out3, decoder_1_out4, decoder_1_out5,
       decoder_1_out6, decoder_1_out7, decoder_1_out8, decoder_1_out9, decoder_1_out10, decoder_1_out11,
       decoder_1_out12, decoder_1_out13, decoder_1_out14, decoder_1_out16, decoder_1_out17, decoder_1_out18,
       decoder_1_out19, decoder_1_out20, decoder_1_out21, decoder_1_out22, decoder_1_out23, decoder_1_out24,
       decoder_1_out25, decoder_1_out26, decoder_1_out27, decoder_1_out28, decoder_1_out29, decoder_1_out30,
       decoder_1_out31, or_1_out;
  wire [4:0] adder_1_out, multiplexer_1_out, subtractor_1_out, subtractor_2_out, subtractor_3_out, TOP_PTR_q;
  wire [15:0] demultiplexer_1_out0, demultiplexer_1_out1, demultiplexer_1_out2, demultiplexer_1_out3,
       demultiplexer_1_out4, demultiplexer_1_out5, demultiplexer_1_out6, demultiplexer_1_out7,
       demultiplexer_1_out8, demultiplexer_1_out9, demultiplexer_1_out10, demultiplexer_1_out11,
       demultiplexer_1_out12, demultiplexer_1_out13, demultiplexer_1_out14, demultiplexer_1_out15,
       demultiplexer_1_out17, demultiplexer_1_out19, demultiplexer_1_out20, demultiplexer_1_out21,
       demultiplexer_1_out22, demultiplexer_1_out24, demultiplexer_1_out25, demultiplexer_1_out26,
       demultiplexer_1_out27, demultiplexer_1_out28, demultiplexer_1_out29, demultiplexer_1_out30,
       demultiplexer_1_out31, register_1_q, register_2_q, register_3_q, register_4_q, register_5_q,
       register_6_q, register_7_q, register_8_q, register_9_q, register_10_q, register_11_q, register_12_q,
       register_13_q, register_14_q, register_15_q, register_16_q, register_18_q, register_19_q,
       register_20_q, register_21_q, register_22_q, register_23_q, register_24_q, register_25_q,
       register_26_q, register_27_q, register_28_q, register_29_q, register_30_q, register_31_q,
       register_32_q, tmp;

  Decoder #(.select(5), .enable("false")) decoder_1 (
    .out0(decoder_1_out0), .out1(decoder_1_out1), .out2(decoder_1_out2), .out3(decoder_1_out3),
    .out4(decoder_1_out4), .out5(decoder_1_out5), .out6(decoder_1_out6), .out7(decoder_1_out7),
    .out8(decoder_1_out8), .out9(decoder_1_out9), .out10(decoder_1_out10), .out11(decoder_1_out11),
    .out12(decoder_1_out12), .out13(decoder_1_out13), .out14(decoder_1_out14), .out15(decoder_1_out14),
    .out16(decoder_1_out16), .out17(decoder_1_out17), .out18(decoder_1_out18), .out19(decoder_1_out19),
    .out20(decoder_1_out20), .out21(decoder_1_out21), .out22(decoder_1_out22), .out23(decoder_1_out23),
    .out24(decoder_1_out24), .out25(decoder_1_out25), .out26(decoder_1_out26), .out27(decoder_1_out27),
    .out28(decoder_1_out28), .out29(decoder_1_out29), .out30(decoder_1_out30), .out31(decoder_1_out31),
    .sel(TOP_PTR_q));
  Subtractor #(.width(5)) subtractor_1 (.a(TOP_PTR_q), .b(5'b00001), .out(subtractor_1_out));  // open: bin, bout
  Adder #(.width(5)) adder_1 (.a(TOP_PTR_q), .b(5'b00001), .out(adder_1_out));  // open: cin, cout
  Multiplexer #(.width(5), .enable("false")) multiplexer_1 (
    .in0(subtractor_1_out), .in1(adder_1_out), .out(multiplexer_1_out), .sel(PUSH));
  or or_1 (or_1_out, PUSH, POP);
  Demultiplexer #(.select(5), .width(16), .enable("false")) demultiplexer_1 (
    .out0(demultiplexer_1_out0), .out1(demultiplexer_1_out1), .out2(demultiplexer_1_out2),
    .out3(demultiplexer_1_out3), .out4(demultiplexer_1_out4), .out5(demultiplexer_1_out5),
    .out6(demultiplexer_1_out6), .out7(demultiplexer_1_out7), .out8(demultiplexer_1_out8),
    .out9(demultiplexer_1_out9), .out10(demultiplexer_1_out10), .out11(demultiplexer_1_out11),
    .out12(demultiplexer_1_out12), .out13(demultiplexer_1_out13), .out14(demultiplexer_1_out14),
    .out15(demultiplexer_1_out15), .out16(demultiplexer_1_out15), .out17(demultiplexer_1_out17),
    .out18(demultiplexer_1_out17), .out19(demultiplexer_1_out19), .out20(demultiplexer_1_out20),
    .out21(demultiplexer_1_out21), .out22(demultiplexer_1_out22), .out23(demultiplexer_1_out22),
    .out24(demultiplexer_1_out24), .out25(demultiplexer_1_out25), .out26(demultiplexer_1_out26),
    .out27(demultiplexer_1_out27), .out28(demultiplexer_1_out28), .out29(demultiplexer_1_out29),
    .out30(demultiplexer_1_out30), .out31(demultiplexer_1_out31), .in(IN), .sel(TOP_PTR_q));
  Register #(.width(5), .Select("low")) TOP_PTR (
    .D(multiplexer_1_out), .en(or_1_out), .Q(TOP_PTR_q), .clk(CLOCK));  // open: clr
  Comparator #(.width(5), .mode("unsigned")) comparator_1 (
    .a(TOP_PTR_q), .b({5{1'b1}}), .gt(OVERFLOW));  // open: eq, lt
  Comparator #(.width(5), .mode("unsigned")) comparator_2 (
    .a(TOP_PTR_q), .b({5{1'b0}}), .eq(HAS_NEXT));  // open: gt, lt
  Register #(.width(16), .Select("low")) register_1 (
    .D(demultiplexer_1_out0), .en(decoder_1_out0), .Q(register_1_q), .clk(CLOCK), .cs(SEL));  // open: clr, preset
  Register #(.width(16), .Select("low")) register_2 (
    .D(demultiplexer_1_out1), .en(decoder_1_out1), .Q(register_2_q), .clk(CLOCK), .cs(SEL));  // open: clr, preset
  Register #(.width(16), .Select("low")) register_3 (
    .D(demultiplexer_1_out2), .en(decoder_1_out2), .Q(register_3_q), .clk(CLOCK), .cs(SEL));  // open: clr, preset
  Register #(.width(16), .Select("low")) register_4 (
    .D(demultiplexer_1_out3), .en(decoder_1_out3), .Q(register_4_q), .clk(CLOCK), .cs(SEL));  // open: clr, preset
  Register #(.width(16), .Select("low")) register_5 (
    .D(demultiplexer_1_out4), .en(decoder_1_out4), .Q(register_5_q), .clk(CLOCK), .cs(SEL));  // open: clr, preset
  Register #(.width(16), .Select("low")) register_6 (
    .D(demultiplexer_1_out5), .en(decoder_1_out5), .Q(register_6_q), .clk(CLOCK), .cs(SEL));  // open: clr, preset
  Register #(.width(16), .Select("low")) register_7 (
    .D(demultiplexer_1_out6), .en(decoder_1_out6), .Q(register_7_q), .clk(CLOCK), .cs(SEL));  // open: clr, preset
  Register #(.width(16), .Select("low")) register_8 (
    .D(demultiplexer_1_out7), .en(decoder_1_out7), .Q(register_8_q), .clk(CLOCK), .cs(SEL));  // open: clr, preset
  Register #(.width(16), .Select("low")) register_9 (
    .D(demultiplexer_1_out8), .en(decoder_1_out8), .Q(register_9_q), .clk(CLOCK), .cs(SEL));  // open: clr, preset
  Register #(.width(16), .Select("low")) register_10 (
    .D(demultiplexer_1_out9), .en(decoder_1_out9), .Q(register_10_q), .clk(CLOCK), .cs(SEL));  // open: clr, preset
  Register #(.width(16), .Select("low")) register_11 (
    .D(demultiplexer_1_out10), .en(decoder_1_out10), .Q(register_11_q), .clk(CLOCK), .cs(SEL));  // open: clr, preset
  Register #(.width(16), .Select("low")) register_12 (
    .D(demultiplexer_1_out11), .en(decoder_1_out11), .Q(register_12_q), .clk(CLOCK), .cs(SEL));  // open: clr, preset
  Register #(.width(16), .Select("low")) register_13 (
    .D(demultiplexer_1_out12), .en(decoder_1_out12), .Q(register_13_q), .clk(CLOCK), .cs(SEL));  // open: clr, preset
  Register #(.width(16), .Select("low")) register_14 (
    .D(demultiplexer_1_out13), .en(decoder_1_out13), .Q(register_14_q), .clk(CLOCK), .cs(SEL));  // open: clr, preset
  Register #(.width(16), .Select("low")) register_15 (
    .D(demultiplexer_1_out14), .en(decoder_1_out14), .Q(register_15_q), .clk(CLOCK), .cs(SEL));  // open: clr, preset
  Register #(.width(16), .Select("low")) register_16 (
    .D(demultiplexer_1_out15), .en(decoder_1_out14), .Q(register_16_q), .clk(CLOCK), .cs(SEL));  // open: clr, preset
  Register #(.width(16), .Select("low")) register_17 (
    .D(demultiplexer_1_out15), .en(decoder_1_out16), .Q(tmp), .clk(CLOCK), .cs(SEL));  // open: clr, preset
  Register #(.width(16), .Select("low")) register_18 (
    .D(demultiplexer_1_out17), .en(decoder_1_out17), .Q(register_18_q), .clk(CLOCK), .cs(SEL));  // open: clr, preset
  Register #(.width(16), .Select("low")) register_19 (
    .D(demultiplexer_1_out17), .en(decoder_1_out18), .Q(register_19_q), .clk(CLOCK), .cs(SEL));  // open: clr, preset
  Register #(.width(16), .Select("low")) register_20 (
    .D(demultiplexer_1_out19), .en(decoder_1_out19), .Q(register_20_q), .clk(CLOCK), .cs(SEL));  // open: clr, preset
  Register #(.width(16), .Select("low")) register_21 (
    .D(demultiplexer_1_out20), .en(decoder_1_out20), .Q(register_21_q), .clk(CLOCK), .cs(SEL));  // open: clr, preset
  Register #(.width(16), .Select("low")) register_22 (
    .D(demultiplexer_1_out21), .en(decoder_1_out21), .Q(register_22_q), .clk(CLOCK), .cs(SEL));  // open: clr, preset
  Register #(.width(16), .Select("low")) register_23 (
    .D(demultiplexer_1_out22), .en(decoder_1_out22), .Q(register_23_q), .clk(CLOCK), .cs(SEL));  // open: clr, preset
  Register #(.width(16), .Select("low")) register_24 (
    .D(demultiplexer_1_out22), .en(decoder_1_out23), .Q(register_24_q), .clk(CLOCK), .cs(SEL));  // open: clr, preset
  Register #(.width(16), .Select("low")) register_25 (
    .D(demultiplexer_1_out24), .en(decoder_1_out24), .Q(register_25_q), .clk(CLOCK), .cs(SEL));  // open: clr, preset
  Register #(.width(16), .Select("low")) register_26 (
    .D(demultiplexer_1_out25), .en(decoder_1_out25), .Q(register_26_q), .clk(CLOCK), .cs(SEL));  // open: clr, preset
  Register #(.width(16), .Select("low")) register_27 (
    .D(demultiplexer_1_out26), .en(decoder_1_out26), .Q(register_27_q), .clk(CLOCK), .cs(SEL));  // open: clr, preset
  Register #(.width(16), .Select("low")) register_28 (
    .D(demultiplexer_1_out27), .en(decoder_1_out27), .Q(register_28_q), .clk(CLOCK), .cs(SEL));  // open: clr, preset
  Register #(.width(16), .Select("low")) register_29 (
    .D(demultiplexer_1_out28), .en(decoder_1_out28), .Q(register_29_q), .clk(CLOCK), .cs(SEL));  // open: clr, preset
  Register #(.width(16), .Select("low")) register_30 (
    .D(demultiplexer_1_out29), .en(decoder_1_out29), .Q(register_30_q), .clk(CLOCK), .cs(SEL));  // open: clr, preset
  Register #(.width(16), .Select("low")) register_31 (
    .D(demultiplexer_1_out30), .en(decoder_1_out30), .Q(register_31_q), .clk(CLOCK), .cs(SEL));  // open: clr, preset
  Register #(.width(16), .Select("low")) register_32 (
    .D(demultiplexer_1_out31), .en(decoder_1_out31), .Q(register_32_q), .clk(CLOCK), .cs(SEL));  // open: clr, preset
  Subtractor #(.width(5)) subtractor_2 (.a(TOP_PTR_q), .b(5'b00010), .out(subtractor_2_out));  // open: bin, bout
  Multiplexer #(.select(5), .width(16), .enable("false")) multiplexer_2 (
    .in0(register_1_q), .in1(register_2_q), .in2(register_3_q), .in3(register_4_q), .in4(register_5_q),
    .in5(register_6_q), .in6(register_7_q), .in7(register_8_q), .in8(register_9_q), .in9(register_10_q),
    .in10(register_11_q), .in11(register_12_q), .in12(register_13_q), .in13(register_14_q),
    .in14(register_15_q), .in15(register_16_q), .in16(tmp), .in17(register_18_q), .in18(register_19_q),
    .in19(register_20_q), .in20(register_21_q), .in21(register_22_q), .in22(register_23_q),
    .in23(register_24_q), .in24(register_25_q), .in25(register_26_q), .in26(register_27_q),
    .in27(register_28_q), .in28(register_29_q), .in29(register_30_q), .in30(register_31_q),
    .in31(register_32_q), .out(NEXT), .sel(subtractor_2_out));
  Subtractor #(.width(5)) subtractor_3 (.a(TOP_PTR_q), .b(5'b00001), .out(subtractor_3_out));  // open: bin, bout
  Multiplexer #(.select(5), .width(16), .enable("false")) multiplexer_3 (
    .in0(register_1_q), .in1(register_2_q), .in2(register_3_q), .in3(register_4_q), .in4(register_5_q),
    .in5(register_6_q), .in6(register_7_q), .in7(register_8_q), .in8(register_9_q), .in9(register_10_q),
    .in10(register_11_q), .in11(register_12_q), .in12(register_13_q), .in13(register_14_q),
    .in14(register_15_q), .in15(register_16_q), .in16(tmp), .in17(register_18_q), .in18(register_19_q),
    .in19(register_20_q), .in20(register_21_q), .in21(register_22_q), .in22(register_23_q),
    .in23(register_24_q), .in24(register_25_q), .in25(register_26_q), .in26(register_27_q),
    .in27(register_28_q), .in28(register_29_q), .in29(register_30_q), .in30(register_31_q),
    .in31(register_32_q), .out(TOP), .sel(subtractor_3_out));
endmodule

module _16bit_stack8 (
  input  [15:0] DATA_IN,
  input  [15:0] CARRY_IN,
  input  PUSH,
  input  POP,
  input  SEL,
  input  CLOCK,
  input  SWAP,
  output [15:0] TOP,
  output [15:0] NEXT,
  output [15:0] LAST,
  output [15:0] CARRY_OUT
);

  wire [15:0] n16bit_stack2_1_last, n16bit_stack2_2_carry_out, n16bit_stack2_2_last,
       n16bit_stack2_3_carry_out, n16bit_stack2_3_last, n16bit_stack2_4_carry_out;

  _16bit_stack2 u_16bit_stack2_1 (
    .DATA_IN(DATA_IN), .CARRY_OUT(CARRY_OUT), .PUSH(PUSH), .POP(POP), .SWAP(SWAP),
    .LAST(n16bit_stack2_1_last), .CARRY_IN(n16bit_stack2_2_carry_out), .TOP(TOP), .NEXT(NEXT), .SEL(SEL),
    .CLOCK(CLOCK));
  _16bit_stack2 u_16bit_stack2_2 (
    .DATA_IN(n16bit_stack2_1_last), .CARRY_OUT(n16bit_stack2_2_carry_out), .PUSH(PUSH), .POP(POP),
    .SWAP(1'b0), .LAST(n16bit_stack2_2_last), .CARRY_IN(n16bit_stack2_3_carry_out), .SEL(SEL), .CLOCK(CLOCK));  // open: TOP, NEXT
  _16bit_stack2 u_16bit_stack2_3 (
    .DATA_IN(n16bit_stack2_2_last), .CARRY_OUT(n16bit_stack2_3_carry_out), .PUSH(PUSH), .POP(POP),
    .SWAP(1'b0), .LAST(n16bit_stack2_3_last), .CARRY_IN(n16bit_stack2_4_carry_out), .SEL(SEL), .CLOCK(CLOCK));  // open: TOP, NEXT
  _16bit_stack2 u_16bit_stack2_4 (
    .DATA_IN(n16bit_stack2_3_last), .CARRY_OUT(n16bit_stack2_4_carry_out), .PUSH(PUSH), .POP(POP),
    .SWAP(1'b0), .LAST(LAST), .CARRY_IN(CARRY_IN), .SEL(SEL), .CLOCK(CLOCK));  // open: TOP, NEXT

  // Other names for the same wires on the sheet: POP_OP = POP; PUSH_OP = PUSH; SWAP_OP = SWAP

  // Notes on the sheet:
  //   16bit-stack8
endmodule

module _16bit_stack2 (
  input  [15:0] DATA_IN,
  input  [15:0] CARRY_IN,
  input  PUSH,
  input  POP,
  input  SWAP,
  input  SEL,
  input  CLOCK,
  output [15:0] TOP,
  output [15:0] NEXT,
  output [15:0] LAST,
  output [15:0] CARRY_OUT
);

  wire and_2_out, and_3_out, and_4_out, BAD_OP, CLOCK_t, controlled_buffer_1_out, MODE, not_1_out, not_3_out,
       or_1_out;
  wire [15:0] controlled_buffer_4_out, controlled_buffer_6_out, controlled_buffer_7_out;

  or or_1 (or_1_out, SWAP, POP, PUSH);
  not not_1 (not_1_out, BAD_OP);
  and and_1 (CLOCK_t, or_1_out, not_1_out, CLOCK);
  and and_2 (and_2_out, PUSH, POP);
  and and_3 (and_3_out, PUSH, SWAP);
  and and_4 (and_4_out, POP, SWAP);
  assign controlled_buffer_1_out = POP ? PUSH : 1'bz;  // Controlled_Buffer controlled_buffer_1
  not not_2 (controlled_buffer_1_out, POP);
  or or_2 (BAD_OP, and_2_out, and_3_out, and_4_out);
  assign MODE = not_3_out ? controlled_buffer_1_out : 1'bz;  // Controlled_Buffer controlled_buffer_2
  assign MODE = SWAP ? 1'b0 : 1'bz;  // Controlled_Buffer controlled_buffer_3
  not not_3 (not_3_out, SWAP);
  Register #(.width(16), .Select("low")) register_1 (
    .D(controlled_buffer_4_out), .Q(TOP), .clk(CLOCK_t), .cs(SEL));  // open: en, clr, preset
  assign controlled_buffer_4_out = MODE ? DATA_IN : 16'bz;  // Controlled_Buffer controlled_buffer_4
  assign controlled_buffer_4_out = ~MODE ? LAST : 16'bz;  // Controlled_Buffer controlled_buffer_5
  assign controlled_buffer_6_out = MODE ? TOP : 16'bz;  // Controlled_Buffer controlled_buffer_6
  assign CARRY_OUT = TOP;  // Buffer buffer_1, 16 bits wide
  assign controlled_buffer_7_out = SWAP ? TOP : 16'bz;  // Controlled_Buffer controlled_buffer_7
  Register #(.width(16), .Select("low")) register_2 (
    .D(controlled_buffer_6_out), .Q(LAST), .clk(CLOCK_t), .cs(SEL));  // open: en, clr, preset
  assign controlled_buffer_6_out = ~MODE ? controlled_buffer_7_out : 16'bz;  // Controlled_Buffer controlled_buffer_8
  assign controlled_buffer_7_out = ~SWAP ? CARRY_IN : 16'bz;  // Controlled_Buffer controlled_buffer_9

  assign NEXT = LAST;

  // Other names for the same wires on the sheet: POP_OP = POP; PUSH_OP = PUSH; SWAP_OP = SWAP
endmodule

module _16bit_stack32 (
  input  [15:0] DATA_IN,
  input  [15:0] CARRY_IN,
  input  PUSH,
  input  POP,
  input  SEL,
  input  CLOCK,
  input  SWAP,
  output [15:0] TOP,
  output [15:0] NEXT,
  output [15:0] LAST,
  output [15:0] CARRY_OUT
);

  wire [15:0] n16bit_stack8_1_last, n16bit_stack8_2_carry_out, n16bit_stack8_2_last,
       n16bit_stack8_3_carry_out, n16bit_stack8_3_last, n16bit_stack8_4_carry_out;

  _16bit_stack8 u_16bit_stack8_1 (
    .DATA_IN(DATA_IN), .CARRY_OUT(CARRY_OUT), .PUSH(PUSH), .POP(POP), .SWAP(SWAP),
    .LAST(n16bit_stack8_1_last), .CARRY_IN(n16bit_stack8_2_carry_out), .TOP(TOP), .NEXT(NEXT), .SEL(SEL),
    .CLOCK(CLOCK));
  _16bit_stack8 u_16bit_stack8_2 (
    .DATA_IN(n16bit_stack8_1_last), .CARRY_OUT(n16bit_stack8_2_carry_out), .PUSH(PUSH), .POP(POP),
    .SWAP(1'b0), .LAST(n16bit_stack8_2_last), .CARRY_IN(n16bit_stack8_3_carry_out), .SEL(SEL), .CLOCK(CLOCK));  // open: TOP, NEXT
  _16bit_stack8 u_16bit_stack8_3 (
    .DATA_IN(n16bit_stack8_2_last), .CARRY_OUT(n16bit_stack8_3_carry_out), .PUSH(PUSH), .POP(POP),
    .SWAP(1'b0), .LAST(n16bit_stack8_3_last), .CARRY_IN(n16bit_stack8_4_carry_out), .SEL(SEL), .CLOCK(CLOCK));  // open: TOP, NEXT
  _16bit_stack8 u_16bit_stack8_4 (
    .DATA_IN(n16bit_stack8_3_last), .CARRY_OUT(n16bit_stack8_4_carry_out), .PUSH(PUSH), .POP(POP),
    .SWAP(1'b0), .LAST(LAST), .CARRY_IN(CARRY_IN), .SEL(SEL), .CLOCK(CLOCK));  // open: TOP, NEXT

  // Other names for the same wires on the sheet: POP_OP = POP; PUSH_OP = PUSH; SWAP_OP = SWAP

  // Notes on the sheet:
  //   16bit-stack32
endmodule

module am08x24arc_stack (
  input  [15:0] DATA_IN,
  input  PUSH,
  input  POP,
  input  SWAP,
  input  SEL,
  input  CLOCK,
  output [15:0] TOP,
  output [15:0] NEXT,
  output [15:0] STORED
);

  wire or_1_out;
  wire [15:0] adder_1_out, multiplexer_1_out, subtractor_1_out;

  _16bit_stack128 u_16bit_stack128_1 (
    .DATA_IN(DATA_IN), .PUSH(PUSH), .POP(POP), .SWAP(SWAP), .CARRY_IN({16{1'b0}}), .TOP(TOP), .NEXT(NEXT),
    .SEL(SEL), .CLOCK(CLOCK));  // open: CARRY_OUT, LAST
  Subtractor #(.width(16)) subtractor_1 (.a(STORED), .b(16'h1), .out(subtractor_1_out));  // open: bin, bout
  Adder #(.width(16)) adder_1 (.a(STORED), .b(16'h1), .out(adder_1_out));  // open: cin, cout
  Multiplexer #(.width(16), .enable("false")) multiplexer_1 (
    .in0(subtractor_1_out), .in1(adder_1_out), .out(multiplexer_1_out), .sel(PUSH));
  Register #(.width(16), .Select("low")) register_1 (
    .D(multiplexer_1_out), .en(or_1_out), .Q(STORED), .clk(CLOCK));  // open: clr
  or or_1 (or_1_out, PUSH, POP);

  // Other names for the same wires on the sheet: POP_OP = POP; PUSH_OP = PUSH; SWAP_OP = SWAP

  // Notes on the sheet:
  //   am08x24arc-stack
endmodule

module _16bit_stack128 (
  input  [15:0] DATA_IN,
  input  [15:0] CARRY_IN,
  input  PUSH,
  input  POP,
  input  SEL,
  input  CLOCK,
  input  SWAP,
  output [15:0] TOP,
  output [15:0] NEXT,
  output [15:0] LAST,
  output [15:0] CARRY_OUT
);

  wire n16bit_stack32_1_p10, n16bit_stack32_1_p11, n16bit_stack32_2_p8, n16bit_stack32_2_p9,
       n16bit_stack32_3_p8, n16bit_stack32_3_p9;

  // _16bit_stack32 16bit_stack32_1: pin names not known; wires that end beside it: DATA_IN, CARRY_OUT, PUSH, POP, SWAP, TOP, SEL, NEXT, CLOCK, n16bit_stack32_1_p10, n16bit_stack32_1_p11
  // _16bit_stack32 16bit_stack32_2: pin names not known; wires that end beside it: n16bit_stack32_1_p10, n16bit_stack32_1_p11, PUSH, POP, 1'b0, SEL, CLOCK, n16bit_stack32_2_p8, n16bit_stack32_2_p9
  // _16bit_stack32 16bit_stack32_3: pin names not known; wires that end beside it: n16bit_stack32_2_p8, n16bit_stack32_2_p9, PUSH, POP, 1'b0, SEL, CLOCK, n16bit_stack32_3_p8, n16bit_stack32_3_p9
  // _16bit_stack32 16bit_stack32_4: pin names not known; wires that end beside it: n16bit_stack32_3_p8, n16bit_stack32_3_p9, PUSH, POP, 1'b0, SEL, CLOCK, LAST, CARRY_IN

  // Other names for the same wires on the sheet: POP_OP = POP; PUSH_OP = PUSH; SWAP_OP = SWAP

  // Notes on the sheet:
  //   16bit-stack128
endmodule

module sandbox (
);

  am08x24arc_main am08x24arc_main_1 ();  // open: in_1, in_2, DATA_BUS_STATUS, RAM_STATUS, out_5, ALU_STATUS, out_7, out_8, out_9, out_10, out_11, out_12
endmodule
